// Logisim project dist-2.circ as structural Verilog: 1 circuit, main circuit main
module main (
  input  A,
  input  B,
  input  C,
  output out_4,
  output out_5
);

  wire and_1_out, or_2_out, or_3_out;

  and and_1 (and_1_out, B, C);
  or or_1 (out_5, A, and_1_out);
  or or_2 (or_2_out, A, B);
  or or_3 (or_3_out, A, C);
  and and_2 (out_4, or_2_out, or_3_out);
endmodule
