// Logisim project univ.circ as structural Verilog
module NOT (
  input  in_1,
  output out_2
);

  nand nand_1 (out_2, in_1, in_1);
endmodule

module AND (
  input  in_1,
  input  in_2,
  output out_3
);

  wire nand_1_out;

  not not_1 (out_3, nand_1_out);
  nand nand_1 (nand_1_out, in_1, in_2);
endmodule

module OR (
  input  in_1,
  input  in_2,
  output out_3
);

  wire not_1_out, not_2_out;

  not not_1 (not_1_out, in_1);
  not not_2 (not_2_out, in_2);
  nand nand_1 (out_3, not_1_out, not_2_out);
endmodule
