// Logisim project alu-1.circ as structural Verilog
module alu_1 (
  input  Carry_In,
  input  Operations,
  input  in_3,
  input  A,
  input  B,
  output Result,
  output Carry_Out
);

  wire and_1_out, fa_1_1_s, or_1_out;

  and and_1 (and_1_out, A, B);
  or or_1 (or_1_out, A, B);
  fa_1 fa_1_1 (.X(A), .Y(B), .Ci(Carry_In), .S(fa_1_1_s), .Co(Carry_Out));
  mux_4i mux_4i_1 (
    .S0(Operations), .S1(in_3), .In0(and_1_out), .In1(or_1_out), .In2(fa_1_1_s), .out_7(Result));  // open: In3
endmodule
