// Logisim project fa-4.circ as structural Verilog
module fa_4 (
  input  Carry_In,
  input  X0,
  input  Y0,
  input  X1,
  input  Y1,
  input  X2,
  input  Y2,
  input  X3,
  input  Y3,
  output S0,
  output S1,
  output S2,
  output S3,
  output Carry_Out
);

  wire fa_1_1_co, fa_1_2_co, fa_1_3_co;

  fa_1 fa_1_1 (.X(X0), .Y(Y0), .Ci(Carry_In), .S(S0), .Co(fa_1_1_co));
  fa_1 fa_1_2 (.X(X1), .Y(Y1), .Ci(fa_1_1_co), .S(S1), .Co(fa_1_2_co));
  fa_1 fa_1_3 (.X(X2), .Y(Y2), .Ci(fa_1_2_co), .S(S2), .Co(fa_1_3_co));
  fa_1 fa_1_4 (.X(X3), .Y(Y3), .Ci(fa_1_3_co), .S(S3), .Co(Carry_Out));
endmodule
