// Logisim project mux-2-8.circ as structural Verilog
module mux_2_8 (
  input  [7:0] in_1,
  input  [7:0] in_2,
  input  S,
  output [7:0] out_4
);

  mux_2_main main_1 (._0(in_1[0]), ._1(in_2[0]), .S(S), .out_4(out_4[0]));
  mux_2_main main_2 (._0(in_1[1]), ._1(in_2[1]), .S(S), .out_4(out_4[1]));
  mux_2_main main_3 (._0(in_1[2]), ._1(in_2[2]), .S(S), .out_4(out_4[2]));
  mux_2_main main_4 (._0(in_1[3]), ._1(in_2[3]), .S(S), .out_4(out_4[3]));
  mux_2_main main_5 (._0(in_1[4]), ._1(in_2[4]), .S(S), .out_4(out_4[4]));
  mux_2_main main_6 (._0(in_1[5]), ._1(in_2[5]), .S(S), .out_4(out_4[5]));
  mux_2_main main_7 (._0(in_1[6]), ._1(in_2[6]), .S(S), .out_4(out_4[6]));
  mux_2_main main_8 (._0(in_1[7]), ._1(in_2[7]), .S(S), .out_4(out_4[7]));

  // Notes on the sheet:
  //   In0
  //   In1
endmodule
