// Logisim project mux-2.circ as structural Verilog: 1 circuit, main circuit main
module main (
  input  _0,
  input  _1,
  input  S,
  output out_4
);

  wire and_1_out, and_2_out, not_1_out;

  not not_1 (not_1_out, S);
  and and_1 (and_1_out, _0, not_1_out);
  and and_2 (and_2_out, _1, S);
  or or_1 (out_4, and_1_out, and_2_out);
endmodule
