// Logisim project mux-4.circ as structural Verilog
module mux_4i (
  input  S0,
  input  S1,
  input  In0,
  input  In1,
  input  In2,
  input  In3,
  output out_7
);

  wire and_1_out, and_2_out, and_3_out, and_4_out, not_1_out, not_2_out;

  not not_1 (not_1_out, S0);
  not not_2 (not_2_out, S1);
  and and_1 (and_1_out, In0, not_2_out, not_1_out);
  and and_2 (and_2_out, In1, not_1_out, S1);
  and and_3 (and_3_out, In2, not_2_out, S0);
  and and_4 (and_4_out, In3, S1, S0, S0);
  or or_1 (out_7, and_1_out, and_2_out, and_3_out, and_4_out);
endmodule

module mux_4ii (
  input  In0,
  input  In1,
  input  In2,
  input  In3,
  input  S0,
  input  S1,
  output out_7
);

  wire main_1_out_4, main_2_out_4;

  mux_2_main main_1 (._0(In0), ._1(In1), .S(S1), .out_4(main_1_out_4));
  mux_2_main main_2 (._0(In2), ._1(In3), .S(S1), .out_4(main_2_out_4));
  mux_2_main main_3 (._0(main_1_out_4), ._1(main_2_out_4), .S(S0), .out_4(out_7));
endmodule
