// Logisim project alu-1bit-slt.circ as structural Verilog
module alu_1bit_slt (
  input  Carry_In,
  input  [1:0] Operations,
  input  AInvert,
  input  BInvert,
  input  A,
  input  B,
  input  Less,
  output Result,
  output Set,
  output Overflow,
  output out_11
);

  wire and_1_out, fa_1_1_s, main_1_out_4, main_2_out_4, not_1_out, not_2_out, or_1_out;

  not not_1 (not_1_out, A);
  Lab__main main_1 (._0(A), ._1(not_1_out), .S(AInvert), .out_4(main_1_out_4));
  not not_2 (not_2_out, B);
  Lab__main main_2 (._0(B), ._1(not_2_out), .S(BInvert), .out_4(main_2_out_4));
  and and_1 (and_1_out, main_1_out_4, main_2_out_4);
  or or_1 (or_1_out, main_1_out_4, main_2_out_4);
  fa_1 fa_1_1 (.X(main_1_out_4), .Y(main_2_out_4), .Ci(Carry_In), .S(fa_1_1_s), .Co(out_11));
  mux_4i mux_4i_1 (
    .S0(Operations[1]), .S1(Operations[0]), .In0(and_1_out), .In1(or_1_out), .In2(fa_1_1_s), .In3(Less),
    .out_7(Result));
  xor xor_1 (Overflow, Carry_In, out_11);
  xor xor_2 (Set, fa_1_1_s, Overflow);

  // Notes on the sheet:
  //   Carry Out
endmodule
