// Logisim project alu-1bit-sub.circ as structural Verilog
module alu_1bit_sub (
  input  BInvert,
  input  Carry_In,
  input  [1:0] Operations,
  input  A,
  input  B,
  output Result,
  output Carry_Out
);

  wire and_1_out, fa_1_1_s, main_1_out_4, not_1_out, or_1_out;

  not not_1 (not_1_out, B);
  Lab__main main_1 (._0(B), ._1(not_1_out), .S(BInvert), .out_4(main_1_out_4));
  and and_1 (and_1_out, A, main_1_out_4);
  or or_1 (or_1_out, A, main_1_out_4);
  fa_1 fa_1_1 (.X(A), .Y(main_1_out_4), .Ci(Carry_In), .S(fa_1_1_s), .Co(Carry_Out));
  mux_4i mux_4i_1 (
    .S0(Operations[1]), .S1(Operations[0]), .In0(and_1_out), .In1(or_1_out), .In2(fa_1_1_s), .out_7(Result));  // open: In3
endmodule
