// Logisim project alu-6bit-mipsbad.circ as structural Verilog: 1 circuit, main circuit main
module main (
  input  [1:0] Operations,
  input  AInvert,
  input  BInvert,
  input  [5:0] A,
  input  [5:0] B,
  input  ZERO,
  output [5:0] RESULT,
  output Equal_Zero,
  output Carry_Out
);

  wire alu_1bit_slt_1_p6, alu_1bit_slt_1_p8, alu_1bit_slt_1_p10, alu_1bit_slt_1_p11, alu_1bit_slt_2_p9,
       alu_1bit_slt_2_p10, alu_1bit_slt_2_p11, alu_1bit_slt_3_p9, alu_1bit_slt_3_p10, alu_1bit_slt_3_p11,
       alu_1bit_slt_4_p9, alu_1bit_slt_4_p10, alu_1bit_slt_4_p11, alu_1bit_slt_5_p9, alu_1bit_slt_5_p10,
       alu_1bit_slt_5_p11, alu_1bit_slt_6_p10;

  // alu_1bit_slt alu_1bit_slt_1: pin names not known; wires that end beside it: Operations[1], Operations[1], BInvert, A[0], B[0], alu_1bit_slt_1_p6, AInvert, alu_1bit_slt_1_p8, RESULT[0], alu_1bit_slt_1_p10, alu_1bit_slt_1_p11
  // alu_1bit_slt alu_1bit_slt_2: pin names not known; wires that end beside it: Operations[1], alu_1bit_slt_1_p8, A[1], B[1], ZERO, AInvert, BInvert, RESULT[1], alu_1bit_slt_2_p9, alu_1bit_slt_2_p10, alu_1bit_slt_2_p11
  // alu_1bit_slt alu_1bit_slt_3: pin names not known; wires that end beside it: Operations[1], alu_1bit_slt_2_p11, A[2], B[2], ZERO, AInvert, BInvert, RESULT[2], alu_1bit_slt_3_p9, alu_1bit_slt_3_p10, alu_1bit_slt_3_p11
  // alu_1bit_slt alu_1bit_slt_4: pin names not known; wires that end beside it: Operations[1], alu_1bit_slt_3_p11, A[3], B[3], ZERO, AInvert, BInvert, RESULT[3], alu_1bit_slt_4_p9, alu_1bit_slt_4_p10, alu_1bit_slt_4_p11
  // alu_1bit_slt alu_1bit_slt_5: pin names not known; wires that end beside it: Operations[1], alu_1bit_slt_4_p11, A[4], B[4], ZERO, AInvert, BInvert, RESULT[4], alu_1bit_slt_5_p9, alu_1bit_slt_5_p10, alu_1bit_slt_5_p11
  // alu_1bit_slt alu_1bit_slt_6: pin names not known; wires that end beside it: Operations[1], alu_1bit_slt_5_p11, A[5], B[5], ZERO, AInvert, BInvert, RESULT[5], alu_1bit_slt_1_p6, alu_1bit_slt_6_p10, Carry_Out
  nor nor_1 (Equal_Zero, RESULT[0], RESULT[1], RESULT[2], RESULT[3], RESULT[4], RESULT[5]);

  assign Operations[0] = Operations[1];

  // Notes on the sheet:
  //   Result 0
  //   Set
  //   Overflow
endmodule
