// Logisim project 2Flop-2Wide-2Read-1Write.circ as structural Verilog: 1 circuit, main circuit main
module main (
  input  Write_Line,
  input  Write_Register_num,
  input  [1:0] Write_Data,
  input  Read_Register__0,
  input  Read_Register__1,
  output [1:0] Register__0,
  output [1:0] Register__1
);

  wire and_1_out, and_2_out, clock_1_out, d_ff_1_q, d_ff_2_q, d_ff_3_q, d_ff_4_q, decoder_1_out0,
       decoder_1_out1, not_1_out, not_2_out, or_1_out, or_2_out;

  Clock clock_1 (.out(clock_1_out));
  Decoder decoder_1 (.out0(decoder_1_out0), .out1(decoder_1_out1), .sel(Write_Register_num));  // open: en
  and and_1 (and_1_out, Write_Line, decoder_1_out0);
  and and_2 (and_2_out, Write_Line, decoder_1_out1);
  not not_1 (not_1_out, and_1_out);
  or or_1 (or_1_out, not_1_out, clock_1_out);
  not not_2 (not_2_out, and_2_out);
  or or_2 (or_2_out, not_2_out, clock_1_out);
  D_Flip_Flop d_ff_1 (.clk(or_1_out), .D(Write_Data[0]), .Q(d_ff_1_q));  // open: Qn, preset, en, reset
  D_Flip_Flop d_ff_2 (.clk(or_1_out), .D(Write_Data[1]), .Q(d_ff_2_q));  // open: Qn, preset, en, reset
  D_Flip_Flop d_ff_3 (.clk(or_2_out), .D(Write_Data[0]), .Q(d_ff_3_q));  // open: Qn, preset, en, reset
  D_Flip_Flop d_ff_4 (.clk(or_2_out), .D(Write_Data[1]), .Q(d_ff_4_q));  // open: Qn, preset, en, reset
  Multiplexer multiplexer_1 (.in0(d_ff_1_q), .in1(d_ff_3_q), .out(Register__0[0]), .sel(Read_Register__0));  // open: en
  Multiplexer multiplexer_2 (.in0(d_ff_2_q), .in1(d_ff_4_q), .out(Register__0[1]), .sel(Read_Register__0));  // open: en
  Multiplexer multiplexer_3 (.in0(d_ff_1_q), .in1(d_ff_3_q), .out(Register__1[0]), .sel(Read_Register__1));  // open: en
  Multiplexer multiplexer_4 (.in0(d_ff_2_q), .in1(d_ff_4_q), .out(Register__1[1]), .sel(Read_Register__1));  // open: en

  // Notes on the sheet:
  //   2Flop-2Wide-2Read-1Write
  //   Clock
  //   Register 0
  //   Register 1
endmodule
