// Logisim project 2Flop-2Wide-2Read.circ as structural Verilog: 1 circuit, main circuit main
module main (
  input  Read_1,
  input  Read_2,
  output [1:0] out_3,
  output [1:0] out_4
);

  wire clock_1_out, d_ff_1_q, d_ff_2_q, d_ff_3_q, d_ff_4_q;

  Clock clock_1 (.out(clock_1_out));
  D_Flip_Flop d_ff_1 (.clk(clock_1_out), .Q(d_ff_1_q));  // open: D, Qn, preset, en, reset
  D_Flip_Flop d_ff_2 (.clk(clock_1_out), .Q(d_ff_2_q));  // open: D, Qn, preset, en, reset
  D_Flip_Flop d_ff_3 (.clk(clock_1_out), .Q(d_ff_3_q));  // open: D, Qn, preset, en, reset
  D_Flip_Flop d_ff_4 (.clk(clock_1_out), .Q(d_ff_4_q));  // open: D, Qn, preset, en, reset
  Multiplexer multiplexer_1 (.in0(d_ff_1_q), .in1(d_ff_3_q), .out(out_3[0]), .sel(Read_1));  // open: en
  Multiplexer multiplexer_2 (.in0(d_ff_2_q), .in1(d_ff_4_q), .out(out_3[1]), .sel(Read_1));  // open: en
  Multiplexer multiplexer_3 (.in0(d_ff_1_q), .in1(d_ff_3_q), .out(out_4[0]), .sel(Read_2));  // open: en
  Multiplexer multiplexer_4 (.in0(d_ff_2_q), .in1(d_ff_4_q), .out(out_4[1]), .sel(Read_2));  // open: en

  // Notes on the sheet:
  //   2Flop-2Wide-2Read
  //   Register 1
  //   Register 2
endmodule
