// Logisim project 4Reg-32Wide-2Read-1Write.circ as structural Verilog: 1 circuit, main circuit main
module main (
  input  RegWrite,
  input  [1:0] WriteReg,
  input  [31:0] in_3,
  input  [1:0] ReadReg1,
  input  [1:0] ReadReg2,
  output [31:0] out_6,
  output [31:0] out_7
);

  wire and_1_out, and_2_out, and_3_out, and_4_out, clock_1_out, decoder_1_out0, decoder_1_out1,
       decoder_1_out2, decoder_1_out3, not_1_out, not_2_out, not_3_out, not_4_out, or_1_out, or_2_out,
       or_3_out, or_4_out;
  wire [31:0] register_1_q, register_2_q, register_3_q, register_4_q;

  Clock clock_1 (.out(clock_1_out));
  Decoder #(.select(2)) decoder_1 (
    .out0(decoder_1_out0), .out1(decoder_1_out1), .out2(decoder_1_out2), .out3(decoder_1_out3), .sel(WriteReg));  // open: en
  and and_1 (and_1_out, RegWrite, decoder_1_out0);
  and and_2 (and_2_out, RegWrite, decoder_1_out1);
  and and_3 (and_3_out, RegWrite, decoder_1_out2);
  and and_4 (and_4_out, RegWrite, decoder_1_out3);
  not not_1 (not_1_out, and_1_out);
  or or_1 (or_1_out, not_1_out, clock_1_out);
  not not_2 (not_2_out, and_2_out);
  or or_2 (or_2_out, not_2_out, clock_1_out);
  not not_3 (not_3_out, and_3_out);
  or or_3 (or_3_out, not_3_out, clock_1_out);
  not not_4 (not_4_out, and_4_out);
  or or_4 (or_4_out, not_4_out, clock_1_out);
  Register #(.width(32)) register_1 (.D(in_3), .Q(register_1_q), .clk(or_1_out));  // open: en, clr
  Register #(.width(32)) register_2 (.D(in_3), .Q(register_2_q), .clk(or_2_out));  // open: en, clr
  Register #(.width(32)) register_3 (.D(in_3), .Q(register_3_q), .clk(or_3_out));  // open: en, clr
  Register #(.width(32)) register_4 (.D(in_3), .Q(register_4_q), .clk(or_4_out));  // open: en, clr
  Multiplexer #(.select(2), .width(32)) multiplexer_1 (
    .in0(register_1_q), .in1(register_2_q), .in2(register_3_q), .in3(register_4_q), .out(out_6),
    .sel(ReadReg1));  // open: en
  Multiplexer #(.select(2), .width(32)) multiplexer_2 (
    .in0(register_1_q), .in1(register_2_q), .in2(register_3_q), .in3(register_4_q), .out(out_7),
    .sel(ReadReg2));  // open: en

  // Notes on the sheet:
  //   WriteData
  //   4Reg-32Wide-2Read-1Write
  //   Clock
  //   Register 0
  //   Register 1
  //   Register 2
  //   Register 3
  //   ReadData1
  //   ReadData2
endmodule
