// Logisim project alu-32bit-mips.circ as structural Verilog: 1 circuit, main circuit ALU-32
module ALU_32 (
  input  Ainvert,
  input  Bnegate,
  input  [1:0] Oper,
  input  [31:0] A,
  input  [31:0] B,
  output Equal_Zero,
  output [31:0] Result,
  output Overflow,
  output CarryOut
);

  wire alu_1bit_slt_1_out_11, alu_1bit_slt_2_out_11, alu_1bit_slt_3_out_11, alu_1bit_slt_4_out_11,
       alu_1bit_slt_5_out_11, alu_1bit_slt_6_out_11, alu_1bit_slt_7_out_11, alu_1bit_slt_8_out_11,
       alu_1bit_slt_9_out_11, alu_1bit_slt_10_out_11, alu_1bit_slt_11_out_11, alu_1bit_slt_12_out_11,
       alu_1bit_slt_13_out_11, alu_1bit_slt_14_out_11, alu_1bit_slt_15_out_11, alu_1bit_slt_16_out_11,
       alu_1bit_slt_17_out_11, alu_1bit_slt_18_out_11, alu_1bit_slt_19_out_11, alu_1bit_slt_20_out_11,
       alu_1bit_slt_21_out_11, alu_1bit_slt_22_out_11, alu_1bit_slt_23_out_11, alu_1bit_slt_24_out_11,
       alu_1bit_slt_25_out_11, alu_1bit_slt_26_out_11, alu_1bit_slt_27_out_11, alu_1bit_slt_28_out_11,
       alu_1bit_slt_29_out_11, alu_1bit_slt_30_out_11, alu_1bit_slt_31_out_11, alu_1bit_slt_32_set, or_1_out;

  alu_1bit_slt alu_1bit_slt_1 (
    .A(A[0]), .B(B[0]), .Less(alu_1bit_slt_32_set), .AInvert(Ainvert), .BInvert(Bnegate), .Carry_In(Bnegate),
    .Operations(Oper), .out_11(alu_1bit_slt_1_out_11), .Result(Result[0]));  // open: Set, Overflow
  alu_1bit_slt alu_1bit_slt_2 (
    .A(A[1]), .B(B[1]), .Less(1'b0), .AInvert(Ainvert), .BInvert(Bnegate), .Carry_In(alu_1bit_slt_1_out_11),
    .Operations(Oper), .out_11(alu_1bit_slt_2_out_11), .Result(Result[1]));  // open: Set, Overflow
  alu_1bit_slt alu_1bit_slt_3 (
    .A(A[2]), .B(B[2]), .Less(1'b0), .AInvert(Ainvert), .BInvert(Bnegate), .Carry_In(alu_1bit_slt_2_out_11),
    .Operations(Oper), .out_11(alu_1bit_slt_3_out_11), .Result(Result[2]));  // open: Set, Overflow
  alu_1bit_slt alu_1bit_slt_4 (
    .A(A[3]), .B(B[3]), .Less(1'b0), .AInvert(Ainvert), .BInvert(Bnegate), .Carry_In(alu_1bit_slt_3_out_11),
    .Operations(Oper), .out_11(alu_1bit_slt_4_out_11), .Result(Result[3]));  // open: Set, Overflow
  alu_1bit_slt alu_1bit_slt_5 (
    .A(A[4]), .B(B[4]), .Less(1'b0), .AInvert(Ainvert), .BInvert(Bnegate), .Carry_In(alu_1bit_slt_4_out_11),
    .Operations(Oper), .out_11(alu_1bit_slt_5_out_11), .Result(Result[4]));  // open: Set, Overflow
  alu_1bit_slt alu_1bit_slt_6 (
    .A(A[5]), .B(B[5]), .Less(1'b0), .AInvert(Ainvert), .BInvert(Bnegate), .Carry_In(alu_1bit_slt_5_out_11),
    .Operations(Oper), .out_11(alu_1bit_slt_6_out_11), .Result(Result[5]));  // open: Set, Overflow
  alu_1bit_slt alu_1bit_slt_7 (
    .A(A[6]), .B(B[6]), .Less(1'b0), .AInvert(Ainvert), .BInvert(Bnegate), .Carry_In(alu_1bit_slt_6_out_11),
    .Operations(Oper), .out_11(alu_1bit_slt_7_out_11), .Result(Result[6]));  // open: Set, Overflow
  alu_1bit_slt alu_1bit_slt_8 (
    .A(A[7]), .B(B[7]), .Less(1'b0), .AInvert(Ainvert), .BInvert(Bnegate), .Carry_In(alu_1bit_slt_7_out_11),
    .Operations(Oper), .out_11(alu_1bit_slt_8_out_11), .Result(Result[7]));  // open: Set, Overflow
  alu_1bit_slt alu_1bit_slt_9 (
    .A(A[8]), .B(B[8]), .Less(1'b0), .AInvert(Ainvert), .BInvert(Bnegate), .Carry_In(alu_1bit_slt_8_out_11),
    .Operations(Oper), .out_11(alu_1bit_slt_9_out_11), .Result(Result[8]));  // open: Set, Overflow
  alu_1bit_slt alu_1bit_slt_10 (
    .A(A[9]), .B(B[9]), .Less(1'b0), .AInvert(Ainvert), .BInvert(Bnegate), .Carry_In(alu_1bit_slt_9_out_11),
    .Operations(Oper), .out_11(alu_1bit_slt_10_out_11), .Result(Result[9]));  // open: Set, Overflow
  alu_1bit_slt alu_1bit_slt_11 (
    .A(A[10]), .B(B[10]), .Less(1'b0), .AInvert(Ainvert), .BInvert(Bnegate),
    .Carry_In(alu_1bit_slt_10_out_11), .Operations(Oper), .out_11(alu_1bit_slt_11_out_11), .Result(Result[10]));  // open: Set, Overflow
  alu_1bit_slt alu_1bit_slt_12 (
    .A(A[11]), .B(B[11]), .Less(1'b0), .AInvert(Ainvert), .BInvert(Bnegate),
    .Carry_In(alu_1bit_slt_11_out_11), .Operations(Oper), .out_11(alu_1bit_slt_12_out_11), .Result(Result[11]));  // open: Set, Overflow
  alu_1bit_slt alu_1bit_slt_13 (
    .A(A[12]), .B(B[12]), .Less(1'b0), .AInvert(Ainvert), .BInvert(Bnegate),
    .Carry_In(alu_1bit_slt_12_out_11), .Operations(Oper), .out_11(alu_1bit_slt_13_out_11), .Result(Result[12]));  // open: Set, Overflow
  alu_1bit_slt alu_1bit_slt_14 (
    .A(A[13]), .B(B[13]), .Less(1'b0), .AInvert(Ainvert), .BInvert(Bnegate),
    .Carry_In(alu_1bit_slt_13_out_11), .Operations(Oper), .out_11(alu_1bit_slt_14_out_11), .Result(Result[13]));  // open: Set, Overflow
  alu_1bit_slt alu_1bit_slt_15 (
    .A(A[14]), .B(B[14]), .Less(1'b0), .AInvert(Ainvert), .BInvert(Bnegate),
    .Carry_In(alu_1bit_slt_14_out_11), .Operations(Oper), .out_11(alu_1bit_slt_15_out_11), .Result(Result[14]));  // open: Set, Overflow
  alu_1bit_slt alu_1bit_slt_16 (
    .A(A[15]), .B(B[15]), .Less(1'b0), .AInvert(Ainvert), .BInvert(Bnegate),
    .Carry_In(alu_1bit_slt_15_out_11), .Operations(Oper), .out_11(alu_1bit_slt_16_out_11), .Result(Result[15]));  // open: Set, Overflow
  alu_1bit_slt alu_1bit_slt_17 (
    .A(A[16]), .B(B[16]), .Less(1'b0), .AInvert(Ainvert), .BInvert(Bnegate),
    .Carry_In(alu_1bit_slt_16_out_11), .Operations(Oper), .out_11(alu_1bit_slt_17_out_11), .Result(Result[16]));  // open: Set, Overflow
  alu_1bit_slt alu_1bit_slt_18 (
    .A(A[17]), .B(B[17]), .Less(1'b0), .AInvert(Ainvert), .BInvert(Bnegate),
    .Carry_In(alu_1bit_slt_17_out_11), .Operations(Oper), .out_11(alu_1bit_slt_18_out_11), .Result(Result[17]));  // open: Set, Overflow
  alu_1bit_slt alu_1bit_slt_19 (
    .A(A[18]), .B(B[18]), .Less(1'b0), .AInvert(Ainvert), .BInvert(Bnegate),
    .Carry_In(alu_1bit_slt_18_out_11), .Operations(Oper), .out_11(alu_1bit_slt_19_out_11), .Result(Result[18]));  // open: Set, Overflow
  alu_1bit_slt alu_1bit_slt_20 (
    .A(A[19]), .B(B[19]), .Less(1'b0), .AInvert(Ainvert), .BInvert(Bnegate),
    .Carry_In(alu_1bit_slt_19_out_11), .Operations(Oper), .out_11(alu_1bit_slt_20_out_11), .Result(Result[19]));  // open: Set, Overflow
  alu_1bit_slt alu_1bit_slt_21 (
    .A(A[20]), .B(B[20]), .Less(1'b0), .AInvert(Ainvert), .BInvert(Bnegate),
    .Carry_In(alu_1bit_slt_20_out_11), .Operations(Oper), .out_11(alu_1bit_slt_21_out_11), .Result(Result[20]));  // open: Set, Overflow
  alu_1bit_slt alu_1bit_slt_22 (
    .A(A[21]), .B(B[21]), .Less(1'b0), .AInvert(Ainvert), .BInvert(Bnegate),
    .Carry_In(alu_1bit_slt_21_out_11), .Operations(Oper), .out_11(alu_1bit_slt_22_out_11), .Result(Result[21]));  // open: Set, Overflow
  alu_1bit_slt alu_1bit_slt_23 (
    .A(A[22]), .B(B[22]), .Less(1'b0), .AInvert(Ainvert), .BInvert(Bnegate),
    .Carry_In(alu_1bit_slt_22_out_11), .Operations(Oper), .out_11(alu_1bit_slt_23_out_11), .Result(Result[22]));  // open: Set, Overflow
  alu_1bit_slt alu_1bit_slt_24 (
    .A(A[23]), .B(B[23]), .Less(1'b0), .AInvert(Ainvert), .BInvert(Bnegate),
    .Carry_In(alu_1bit_slt_23_out_11), .Operations(Oper), .out_11(alu_1bit_slt_24_out_11), .Result(Result[23]));  // open: Set, Overflow
  alu_1bit_slt alu_1bit_slt_25 (
    .A(A[24]), .B(B[24]), .Less(1'b0), .AInvert(Ainvert), .BInvert(Bnegate),
    .Carry_In(alu_1bit_slt_24_out_11), .Operations(Oper), .out_11(alu_1bit_slt_25_out_11), .Result(Result[24]));  // open: Set, Overflow
  alu_1bit_slt alu_1bit_slt_26 (
    .A(A[25]), .B(B[25]), .Less(1'b0), .AInvert(Ainvert), .BInvert(Bnegate),
    .Carry_In(alu_1bit_slt_25_out_11), .Operations(Oper), .out_11(alu_1bit_slt_26_out_11), .Result(Result[25]));  // open: Set, Overflow
  alu_1bit_slt alu_1bit_slt_27 (
    .A(A[26]), .B(B[26]), .Less(1'b0), .AInvert(Ainvert), .BInvert(Bnegate),
    .Carry_In(alu_1bit_slt_26_out_11), .Operations(Oper), .out_11(alu_1bit_slt_27_out_11), .Result(Result[26]));  // open: Set, Overflow
  alu_1bit_slt alu_1bit_slt_28 (
    .A(A[27]), .B(B[27]), .Less(1'b0), .AInvert(Ainvert), .BInvert(Bnegate),
    .Carry_In(alu_1bit_slt_27_out_11), .Operations(Oper), .out_11(alu_1bit_slt_28_out_11), .Result(Result[27]));  // open: Set, Overflow
  alu_1bit_slt alu_1bit_slt_29 (
    .A(A[28]), .B(B[28]), .Less(1'b0), .AInvert(Ainvert), .BInvert(Bnegate),
    .Carry_In(alu_1bit_slt_28_out_11), .Operations(Oper), .out_11(alu_1bit_slt_29_out_11), .Result(Result[28]));  // open: Set, Overflow
  alu_1bit_slt alu_1bit_slt_30 (
    .A(A[29]), .B(B[29]), .Less(1'b0), .AInvert(Ainvert), .BInvert(Bnegate),
    .Carry_In(alu_1bit_slt_29_out_11), .Operations(Oper), .out_11(alu_1bit_slt_30_out_11), .Result(Result[29]));  // open: Set, Overflow
  alu_1bit_slt alu_1bit_slt_31 (
    .A(A[30]), .B(B[30]), .Less(1'b0), .AInvert(Ainvert), .BInvert(Bnegate),
    .Carry_In(alu_1bit_slt_30_out_11), .Operations(Oper), .out_11(alu_1bit_slt_31_out_11), .Result(Result[30]));  // open: Set, Overflow
  alu_1bit_slt alu_1bit_slt_32 (
    .A(A[31]), .B(B[31]), .Less(1'b0), .AInvert(Ainvert), .BInvert(Bnegate),
    .Carry_In(alu_1bit_slt_31_out_11), .Operations(Oper), .out_11(CarryOut), .Result(Result[31]),
    .Set(alu_1bit_slt_32_set), .Overflow(Overflow));
  or or_1 (or_1_out, Result[0], Result[1], Result[2], Result[3], Result[4], Result[5], Result[6], Result[7], Result[8], Result[9], Result[10], Result[11], Result[12], Result[13], Result[14], Result[15], Result[16], Result[17], Result[18], Result[19], Result[20], Result[21], Result[22], Result[23], Result[24], Result[25], Result[26], Result[27], Result[28], Result[29], Result[30], Result[31]);
  not not_1 (Equal_Zero, or_1_out);

  // Notes on the sheet:
  //   alue-32bits-mips
  //   Less
endmodule
