// Logisim project Replace.circ as structural Verilog: 1 circuit, main circuit main
module main (
  input  Write_Line,
  input  Write_Register_num,
  input  [1:0] Write_Data,
  input  Read_Register__0,
  input  Read_Register__1,
  output [1:0] Register__0,
  output [1:0] Register__1
);

  wire and_1_out, and_2_out, clock_1_out, decoder_1_out0, decoder_1_out1, not_1_out, not_2_out, or_1_out,
       or_2_out;
  wire [1:0] register_1_q, register_2_q;

  Clock clock_1 (.out(clock_1_out));
  Decoder decoder_1 (.out0(decoder_1_out0), .out1(decoder_1_out1), .sel(Write_Register_num));  // open: en
  and and_1 (and_1_out, Write_Line, decoder_1_out0);
  and and_2 (and_2_out, Write_Line, decoder_1_out1);
  not not_1 (not_1_out, and_1_out);
  or or_1 (or_1_out, not_1_out, clock_1_out);
  not not_2 (not_2_out, and_2_out);
  or or_2 (or_2_out, not_2_out, clock_1_out);
  Register #(.width(2)) register_1 (.D(Write_Data), .Q(register_1_q), .clk(or_1_out));  // open: en, clr
  Register #(.width(2)) register_2 (.D(Write_Data), .Q(register_2_q), .clk(or_2_out));  // open: en, clr
  Multiplexer #(.width(2)) multiplexer_1 (
    .in0(register_1_q), .in1(register_2_q), .out(Register__0), .sel(Read_Register__0));  // open: en
  Multiplexer #(.width(2)) multiplexer_2 (
    .in0(register_1_q), .in1(register_2_q), .out(Register__1), .sel(Read_Register__1));  // open: en

  // Notes on the sheet:
  //   Clock
  //   Register 0
  //   Register 1
endmodule
