// Logisim project ALU-Control.circ as structural Verilog: 1 circuit, main circuit ALU-Control
module ALU_Control (
  input  [1:0] ALUOp,
  input  F3,
  input  F2,
  input  F1,
  input  F0,
  output [2:0] ALUCntl
);

  wire and_1_out, not_1_out, not_2_out, or_1_out;

  and and_1 (and_1_out, ALUOp[1], F1);
  or or_1 (or_1_out, F3, F0);
  not not_1 (not_1_out, ALUOp[1]);
  not not_2 (not_2_out, F2);
  or or_2 (ALUCntl[2], ALUOp[0], and_1_out);
  or or_3 (ALUCntl[1], not_1_out, not_2_out);
  and and_2 (ALUCntl[0], ALUOp[1], or_1_out);

  // Notes on the sheet:
  //   F[5-0]
  //   ALU CONTROL
  //   ALUOp0
  //   ALUOp1
  //   BNegate
  //   Op1
  //   Op0
endmodule
