// Logisim project Data-Memory.circ as structural Verilog: 1 circuit, main circuit Data-Memory
module Data_Memory (
  input  [31:0] Address,
  input  [31:0] Write_Data,
  input  Mem_Write,
  input  in_4,
  output [31:0] Read_Data
);

  wire not_1_out;

  RAM #(.addrWidth(6), .dataWidth(32), .bus("separate")) ram_1 (
    .addr(Address[7:2]), .din(Write_Data), .data(Read_Data), .str(Mem_Write), .clk(not_1_out));  // open: sel, ld, clr
  not not_1 (not_1_out, in_4);
endmodule
