// Logisim project Instruction-Memory.circ as structural Verilog: 1 circuit, main circuit Instruction-Memory
module Instruction_Memory (
  input  [31:0] in_1,
  output [31:0] out_2
);

  ROM #(.addrWidth(5), .dataWidth(32)) rom_1 (.addr(in_1[6:2]), .data(out_2));  // open: sel
endmodule
