// Logisim project Main-Control.circ as structural Verilog: 1 circuit, main circuit Main-Control
module Main_Control (
  input  OP5,
  input  OP4,
  input  OP3,
  input  OP2,
  input  OP1,
  input  OP0,
  output MemWrite,
  output Branch,
  output [1:0] ALUOp,
  output MemToReg,
  output ALUSrc,
  output RegWrite,
  output RegDst
);

  wire not_1_out, not_2_out, not_3_out, not_4_out, not_5_out, not_6_out, not_7_out, not_8_out, not_9_out,
       not_10_out, not_11_out, not_12_out, not_13_out, not_14_out, not_15_out, not_16_out;

  not not_1 (not_1_out, OP1);
  not not_2 (not_2_out, OP5);
  not not_3 (not_3_out, OP2);
  not not_4 (not_4_out, OP4);
  not not_5 (not_5_out, OP3);
  and and_1 (ALUOp[1], not_2_out, not_4_out, not_5_out, not_3_out, not_1_out, not_8_out);
  not not_6 (not_6_out, OP4);
  not not_7 (not_7_out, OP2);
  not not_8 (not_8_out, OP0);
  not not_9 (not_9_out, OP3);
  and and_2 (MemToReg, OP5, not_6_out, not_9_out, not_7_out, OP1, OP0);
  not not_10 (not_10_out, OP4);
  and and_3 (MemWrite, OP5, not_10_out, OP3, not_12_out, OP1, OP0);
  not not_11 (not_11_out, OP3);
  not not_12 (not_12_out, OP2);
  not not_13 (not_13_out, OP4);
  not not_14 (not_14_out, OP5);
  not not_15 (not_15_out, OP0);
  not not_16 (not_16_out, OP1);
  and and_4 (ALUOp[0], not_14_out, not_13_out, not_11_out, OP2, not_16_out, not_15_out);
  or or_1 (ALUSrc, MemToReg, MemWrite);
  or or_2 (RegWrite, ALUOp[1], MemToReg);

  assign Branch = ALUOp[0];
  assign RegDst = ALUOp[1];

  // Notes on the sheet:
  //   MAIN CONTROL
  //   Instructions: 31-26
endmodule
