// Logisim project PC.circ as structural Verilog: 1 circuit, main circuit PC
module PC (
  input  [31:0] Data_In,
  input  in_2,
  output [31:0] Data_Out
);

  Register #(.width(32), .trigger("falling")) register_1 (.D(Data_In), .Q(Data_Out), .clk(in_2));  // open: en, clr
endmodule
