// Logisim project finaleCpoy.circ as structural Verilog: 1 circuit, main circuit main
module main (
);

  wire ALU_equal_zero, and_1_out, clock_1_out, Main_Control_alusrc, Main_Control_branch,
       Main_Control_memtoreg, Main_Control_memwrite, Main_Control_regdst, Main_Control_regwrite;
  wire [1:0] Alu_Control_alucntl, Main_Control_aluop;
  wire [2:2] Alu_Control_alucntl_2;
  wire [4:0] multiplexer_1_out;
  wire [31:0] Add_2_result, Add_result, ALU_result, Data_Memory_read_data, Instruction_Memory_out_2,
       multiplexer_2_out, multiplexer_3_out, multiplexer_4_out, PC_data_out, Registers_out_7,
       Registers_out_8, Shift_Left_shifted_result, Sign_Extend_out_2;

  Clock clock_1 (.out(clock_1_out));
  PC PC (.Data_In(multiplexer_4_out), .in_2(clock_1_out), .Data_Out(PC_data_out));
  Adder_32 Add (.A(32'h4), .B(PC_data_out), .Result(Add_result));  // open: CarryOut, Equal_Zero, Overflow
  Instruction_Memory Instruction_Memory (.in_1(PC_data_out), .out_2(Instruction_Memory_out_2));
  Multiplexer #(.width(5)) multiplexer_1 (
    .in0(Instruction_Memory_out_2[20:16]), .in1(Instruction_Memory_out_2[15:11]), .out(multiplexer_1_out),
    .sel(Main_Control_regdst));  // open: en
  Main_Control Main_Control (
    .OP5(Instruction_Memory_out_2[31]), .OP4(Instruction_Memory_out_2[30]),
    .OP3(Instruction_Memory_out_2[29]), .OP2(Instruction_Memory_out_2[28]),
    .OP1(Instruction_Memory_out_2[27]), .OP0(Instruction_Memory_out_2[26]), .MemWrite(Main_Control_memwrite),
    .Branch(Main_Control_branch), .ALUOp(Main_Control_aluop), .MemToReg(Main_Control_memtoreg),
    .ALUSrc(Main_Control_alusrc), .RegWrite(Main_Control_regwrite), .RegDst(Main_Control_regdst));
  Registers Registers (
    .WriteReg(multiplexer_1_out[1:0]), .in_4(multiplexer_3_out), .ReadReg1(Instruction_Memory_out_2[22:21]),
    .ReadReg2(Instruction_Memory_out_2[17:16]), .Clock(clock_1_out), .RegWrite(Main_Control_regwrite),
    .out_7(Registers_out_7), .out_8(Registers_out_8));
  Multiplexer #(.width(32)) multiplexer_2 (
    .in0(Registers_out_8), .in1(Sign_Extend_out_2), .out(multiplexer_2_out), .sel(Main_Control_alusrc));  // open: en
  sign_extend Sign_Extend (.in_1(Instruction_Memory_out_2[15:0]), .out_2(Sign_Extend_out_2));
  Multiplexer #(.width(32)) multiplexer_3 (
    .in0(ALU_result), .in1(Data_Memory_read_data), .out(multiplexer_3_out), .sel(Main_Control_memtoreg));  // open: en
  shift_left Shift_Left (.Data_to_be_shifted(Sign_Extend_out_2), .Shifted_Result(Shift_Left_shifted_result));
  ALU ALU (
    .A(Registers_out_7), .B(multiplexer_2_out), .Bnegate(Alu_Control_alucntl_2[2]),
    .Oper(Alu_Control_alucntl), .Equal_Zero(ALU_equal_zero), .Result(ALU_result));  // open: CarryOut, Overflow
  ALU_Control Alu_Control (
    .F3(Instruction_Memory_out_2[3]), .F2(Instruction_Memory_out_2[2]), .F1(Instruction_Memory_out_2[1]),
    .F0(Instruction_Memory_out_2[0]), .ALUOp(Main_Control_aluop),
    .ALUCntl({Alu_Control_alucntl_2[2], Alu_Control_alucntl}));
  Adder_32 Add_2 (
    .A(Add_result), .B(Shift_Left_shifted_result), .Result(Add_2_result));  // open: CarryOut, Equal_Zero, Overflow
  Data_Memory Data_Memory (
    .Address(ALU_result), .Write_Data(Registers_out_8), .Mem_Write(Main_Control_memwrite),
    .in_4(clock_1_out), .Read_Data(Data_Memory_read_data));
  Multiplexer #(.width(32)) multiplexer_4 (
    .in0(Add_result), .in1(Add_2_result), .out(multiplexer_4_out), .sel(and_1_out));  // open: en
  and and_1 (and_1_out, Main_Control_branch, ALU_equal_zero);

  // Notes on the sheet:
  //   RegDst
endmodule
