// Logisim project shift-left.circ as structural Verilog: 1 circuit, main circuit shift-left
module shift_left (
  input  [31:0] Data_to_be_shifted,
  output [31:0] Shifted_Result
);

  Shifter #(.width(32)) shifter_1 (.in(Data_to_be_shifted), .\dist (5'b00010), .out(Shifted_Result));

  // Notes on the sheet:
  //   Shift 2
endmodule
